# Fritzing sketch homework1 (saved by Fritzing 0.9.3b)
breadboards: 1

parts:
  Part1 = Arduino Uno (Rev3)
  J1 = Basic Servo
  S1 = Pushbutton [package="[THT]"]
  R1 = Resistor [tolerance=±5% resistance=220 package=THT]

nets:
  N1: Part1.D9_PWM, J1.pulse
  N2: Part1.D2, S1.Pin_1, S1.Pin_2, R1.Pin_0
  5V: Part1.5V, J1.vcc, S1.Pin_3, S1.Pin_4
  GND: Part1.GND, J1.gnd, R1.Pin_1
